# Fritzing sketch teensy-breadboard (saved by Fritzing 1.0.8)
breadboards: 1

parts:
  Nokia_5110_LCD_Module1 = Nokia 5110 LCD
  Mod1 = Raspberry Pi Pico
  Mod2 = Passive Buzzer
  KEYPAD1 = Membrane Matrix Keypad

nets:
  N1: Nokia_5110_LCD_Module1.VCC, Nokia_5110_LCD_Module1.VCC_(out), Mod1.pin_27
  N2: Nokia_5110_LCD_Module1.GND, Nokia_5110_LCD_Module1.GND_(out), Mod1.pin_22
  N3: Nokia_5110_LCD_Module1.SCE, Nokia_5110_LCD_Module1.SCE_(out), Mod1.pin_26
  N4: Nokia_5110_LCD_Module1.RST, Nokia_5110_LCD_Module1.RST_(out), Mod1.pin_25
  N5: Nokia_5110_LCD_Module1.D/C, Nokia_5110_LCD_Module1.D/C_(out), Mod1.pin_24
  N6: Nokia_5110_LCD_Module1.DN(MODI)_(out), Mod1.pin_36, Mod2.NC
  N7: Nokia_5110_LCD_Module1.LED_(out), Mod1.pin_3, Mod1.pin_8, Mod1.pin_13, Mod1.pin_18, Mod1.pin_23, Mod1.pin_28, Mod1.pin_33, Mod1.pin_38, Mod1.pin_42, Mod2.-
  N8: Mod1.pin_5, KEYPAD1.5
  N9: Mod1.pin_6, KEYPAD1.6
  N10: Mod1.pin_7, KEYPAD1.7
  N11: Mod1.pin_9, KEYPAD1.1
  N12: Mod1.pin_10, KEYPAD1.2
  N13: Mod1.pin_11, KEYPAD1.3
  N14: Mod1.pin_12, KEYPAD1.4
  N15: Mod1.pin_20, Mod2.S

notes:
  3V3
  GP21
  GP20
  GP19
  GP18
  GP17
  RST
  CE
  DC
  DIN
  CLK
  VCC
  GND
  LIGHT
  GP15
  GP6
  GP3
  GP4
  GP5
  GP7
  GP8
  GP9
  BUZZER
  COL1
  COL3
  COL2
  ROW2
  ROW3
  ROW1
  ROW4
  This pinout is based on the display module I have, each vendor uses a different pinout

custom parts:
  Nokia 5110 LCD: Nokia 5110 Graphic 84*48 LCD module such as the Sparkfun LCD-10168 or the clones from Ebay. There is example code for the Arduino available from the Sparkfun site in https://learn.sparkfun.com/tutorials/graphic-lcd-hookup-guide This is a 3.3V device, if you are running it from a 5V micro you need a 5V tolorant level translator such as the 74ahc367 to protect the signal imputs. Rafa G. did a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
  Raspberry Pi Pico: Raspberry Pi Pico. Based around the RP2040 microcontroller the Pico is a low cost microcontroller device bringing Raspberry Pi quality, cost, and easy of use to the microcontroller space. Jan 2021, Split part in to two versions: tht (this one) and SMD. This one will drill holes for a .1 in header in pcb to allow plugging in the module as well as providing pads to solder the module to the top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
  Membrane Matrix Keypad: Membrane Matrix 3x4 Keypad
